// Logisim project RTC.circ as structural Verilog: 20 circuits, main circuit main
module main (
);

  wire _0_005sec, _0_05sec, _0_5sec, _1Hz, _4Hz, _5sec, adjust_en, adjust_out, advance_time, clock_1_out,
       clock_2_out, clock_3_out, clock_4_out, clock_5_out, display_control_1_hours_ssd_a,
       display_control_1_hours_ssd_b, display_control_1_hours_ssd_c, display_control_1_hours_ssd_d,
       display_control_1_hours_ssd_e, display_control_1_hours_ssd_f, display_control_1_hours_ssd_g,
       display_control_1_minutes_ssd_a, display_control_1_minutes_ssd_b, display_control_1_minutes_ssd_c,
       display_control_1_minutes_ssd_d, display_control_1_minutes_ssd_e, display_control_1_minutes_ssd_f,
       display_control_1_minutes_ssd_g, display_control_1_month_days_ssd_a,
       display_control_1_month_days_ssd_b, display_control_1_month_days_ssd_c,
       display_control_1_month_days_ssd_d, display_control_1_month_days_ssd_e,
       display_control_1_month_days_ssd_f, display_control_1_month_days_ssd_g,
       display_control_1_months_ssd_a, display_control_1_months_ssd_b, display_control_1_months_ssd_c,
       display_control_1_months_ssd_d, display_control_1_months_ssd_e, display_control_1_months_ssd_f,
       display_control_1_months_ssd_g, display_control_1_seconds_ssd_a, display_control_1_seconds_ssd_b,
       display_control_1_seconds_ssd_c, display_control_1_seconds_ssd_d, display_control_1_seconds_ssd_e,
       display_control_1_seconds_ssd_f, display_control_1_seconds_ssd_g, display_control_1_tens_hours_ssd_a,
       display_control_1_tens_hours_ssd_b, display_control_1_tens_hours_ssd_c,
       display_control_1_tens_hours_ssd_d, display_control_1_tens_hours_ssd_e,
       display_control_1_tens_hours_ssd_f, display_control_1_tens_hours_ssd_g,
       display_control_1_tens_minutes_ssd_a, display_control_1_tens_minutes_ssd_b,
       display_control_1_tens_minutes_ssd_c, display_control_1_tens_minutes_ssd_d,
       display_control_1_tens_minutes_ssd_e, display_control_1_tens_minutes_ssd_f,
       display_control_1_tens_minutes_ssd_g, display_control_1_tens_month_days_ssd_a,
       display_control_1_tens_month_days_ssd_b, display_control_1_tens_month_days_ssd_c,
       display_control_1_tens_month_days_ssd_d, display_control_1_tens_month_days_ssd_e,
       display_control_1_tens_month_days_ssd_f, display_control_1_tens_month_days_ssd_g,
       display_control_1_tens_months_ssd_a, display_control_1_tens_months_ssd_b,
       display_control_1_tens_months_ssd_c, display_control_1_tens_months_ssd_d,
       display_control_1_tens_months_ssd_e, display_control_1_tens_months_ssd_f,
       display_control_1_tens_months_ssd_g, display_control_1_tens_seconds_ssd_a,
       display_control_1_tens_seconds_ssd_b, display_control_1_tens_seconds_ssd_c,
       display_control_1_tens_seconds_ssd_d, display_control_1_tens_seconds_ssd_e,
       display_control_1_tens_seconds_ssd_f, display_control_1_tens_seconds_ssd_g, mode_out, set_out,
       time_advance_logic_1_centuries_set_en, time_advance_logic_1_day_of_month_set_en,
       time_advance_logic_1_hours_set_en, time_advance_logic_1_minutes_set_en,
       time_advance_logic_1_months_set_en, time_advance_logic_1_week_day_set_en,
       time_advance_logic_1_years_set_en;
  wire [2:0] adjust_select, time_advance_logic_1_week_day_set, week_day;
  wire [3:0] month, time_advance_logic_1_months_set;
  wire [4:0] display_control_1_week_day_l0, display_control_1_week_day_l1, display_control_1_week_day_l2,
       display_control_1_week_day_l3, display_control_1_week_day_l4, display_control_1_week_day_l5,
       display_control_1_week_day_l6, display_control_1_week_day_l7, display_control_1_week_day_l8,
       display_control_1_week_day_l9, display_control_1_week_day_l10, display_control_1_week_day_l11,
       display_control_1_week_day_l12, display_control_1_week_day_l13, display_control_1_week_day_l14,
       display_control_1_week_day_l15, display_control_1_week_day_l16, hours, month_day,
       time_advance_logic_1_day_of_month_set, time_advance_logic_1_hours_set;
  wire [5:0] minutes, seconds, time_advance_logic_1_minutes_set, time_advance_logic_1_seconds_set;
  wire [6:0] century, time_advance_logic_1_centuries_set, time_advance_logic_1_years_set,
       timer_1_hundredths_seconds_timer, timer_1_minutes_timer, timer_1_seconds_timer, year;

  clock_conditioning clock_conditioning_1 (
    .clock(clock_1_out), ._1Hz(_1Hz), ._4Hz(_4Hz), .half_hundreds_seconds(_0_005sec),
    .half_tens_seconds(_0_05sec), .half_sec(_0_5sec), ._5_seconds(_5sec));
  Clock clock_1 (.out(clock_1_out));
  time_advance_logic time_advance_logic_1 (
    .seconds(seconds), .minutes(minutes), .hours(hours), .day_of_month(month_day), .months(month),
    .years(year), .centuries(century), .seconds_set(time_advance_logic_1_seconds_set),
    .minutes_set(time_advance_logic_1_minutes_set), .hours_set(time_advance_logic_1_hours_set),
    .day_of_month_set(time_advance_logic_1_day_of_month_set), .months_set(time_advance_logic_1_months_set),
    .years_set(time_advance_logic_1_years_set), .centuries_set(time_advance_logic_1_centuries_set),
    .adjust_en(adjust_en), .adjust_control_reg(adjust_select), .set(advance_time),
    .minutes_set_en(time_advance_logic_1_minutes_set_en), .hours_set_en(time_advance_logic_1_hours_set_en),
    .day_of_month_set_en(time_advance_logic_1_day_of_month_set_en),
    .months_set_en(time_advance_logic_1_months_set_en), .years_set_en(time_advance_logic_1_years_set_en),
    .centuries_set_en(time_advance_logic_1_centuries_set_en), .week_day(week_day),
    .week_day_set(time_advance_logic_1_week_day_set), .week_day_set_en(time_advance_logic_1_week_day_set_en));
  Button set (.out(set_out));
  Button mode (.out(mode_out));
  Button adjust (.out(adjust_out));
  Clock clock_2 (.out(clock_2_out));
  Clock clock_3 (.out(clock_3_out));
  state_control state_control_1 (
    .clk(clock_2_out), .mode(mode_out), .adjust(adjust_out), .time_set_mode(adjust_en),
    .adjust_state_reg(adjust_select), .set(set_out), .set_out(advance_time));  // open: mode_encode
  time_data time_data_1 (
    .years_set(time_advance_logic_1_years_set), .years_set_en(time_advance_logic_1_years_set_en),
    .months_set(time_advance_logic_1_months_set), .months_set_en(time_advance_logic_1_months_set_en),
    .hours_set(time_advance_logic_1_hours_set), .hours_set_en(time_advance_logic_1_hours_set_en),
    .minutes_set(time_advance_logic_1_minutes_set), .minutes_set_en(time_advance_logic_1_minutes_set_en),
    .seconds_set(time_advance_logic_1_seconds_set), .seconds_set_en(_0_5sec), .clk(clock_3_out),
    .years_out(year), .months_out(month), .hours_out(hours), .minutes_out(minutes), .seconds_out(seconds),
    .day_of_week_set_en(time_advance_logic_1_week_day_set_en),
    .day_of_week_set(time_advance_logic_1_week_day_set), .day_of_week_out(week_day),
    .day_of_month_out(month_day), .day_of_month_set(time_advance_logic_1_day_of_month_set),
    .day_of_month_set_en(time_advance_logic_1_day_of_month_set_en),
    .centuries_set(time_advance_logic_1_centuries_set), .centuries_out(century),
    .centuries_set_en(time_advance_logic_1_centuries_set_en), .adjust_control_reg(adjust_select),
    .adjust_en(adjust_en), .set(advance_time));
  Clock clock_4 (.out(clock_4_out));
  Clock clock_5 (.out(clock_5_out));
  timer timer_1 (
    .clk(clock_4_out), .half_hundredth_seconds(_0_005sec),
    .hundredths_seconds_timer(timer_1_hundredths_seconds_timer), .seconds_timer(timer_1_seconds_timer),
    .minutes_timer(timer_1_minutes_timer));  // open: reset
  _7_Segment_Display u_7_segment_display_1 (
    .g(display_control_1_tens_hours_ssd_g), .f(display_control_1_tens_hours_ssd_f),
    .a(display_control_1_tens_hours_ssd_a), .b(display_control_1_tens_hours_ssd_b),
    .e(display_control_1_tens_hours_ssd_e), .d(display_control_1_tens_hours_ssd_d),
    .c(display_control_1_tens_hours_ssd_c));  // open: dp
  // Probe on timer_1_hundredths_seconds_timer
  // Probe on timer_1_seconds_timer
  // Probe on timer_1_minutes_timer
  _7_Segment_Display u_7_segment_display_2 (
    .g(display_control_1_hours_ssd_g), .f(display_control_1_hours_ssd_f), .a(display_control_1_hours_ssd_a),
    .b(display_control_1_hours_ssd_b), .e(display_control_1_hours_ssd_e), .d(display_control_1_hours_ssd_d),
    .c(display_control_1_hours_ssd_c));  // open: dp
  DotMatrix #(.matrixcols(17), .matrixrows(5)) dotmatrix_1 (
    .col0(display_control_1_week_day_l0), .col1(display_control_1_week_day_l1),
    .col2(display_control_1_week_day_l2), .col3(display_control_1_week_day_l3),
    .col4(display_control_1_week_day_l4), .col5(display_control_1_week_day_l5),
    .col6(display_control_1_week_day_l6), .col7(display_control_1_week_day_l7),
    .col8(display_control_1_week_day_l8), .col9(display_control_1_week_day_l9),
    .col10(display_control_1_week_day_l10), .col11(display_control_1_week_day_l11),
    .col12(display_control_1_week_day_l12), .col13(display_control_1_week_day_l13),
    .col14(display_control_1_week_day_l14), .col15(display_control_1_week_day_l15),
    .col16(display_control_1_week_day_l16));
  _7_Segment_Display u_7_segment_display_3 (
    .g(display_control_1_tens_months_ssd_g), .f(display_control_1_tens_months_ssd_f),
    .a(display_control_1_tens_months_ssd_a), .b(display_control_1_tens_months_ssd_b),
    .e(display_control_1_tens_months_ssd_e), .d(display_control_1_tens_months_ssd_d),
    .c(display_control_1_tens_months_ssd_c));  // open: dp
  _7_Segment_Display u_7_segment_display_4 (
    .g(display_control_1_tens_minutes_ssd_g), .f(display_control_1_tens_minutes_ssd_f),
    .a(display_control_1_tens_minutes_ssd_a), .b(display_control_1_tens_minutes_ssd_b),
    .e(display_control_1_tens_minutes_ssd_e), .d(display_control_1_tens_minutes_ssd_d),
    .c(display_control_1_tens_minutes_ssd_c));  // open: dp
  _7_Segment_Display u_7_segment_display_5 (
    .g(display_control_1_minutes_ssd_g), .f(display_control_1_minutes_ssd_f),
    .a(display_control_1_minutes_ssd_a), .b(display_control_1_minutes_ssd_b),
    .e(display_control_1_minutes_ssd_e), .d(display_control_1_minutes_ssd_d),
    .c(display_control_1_minutes_ssd_c));  // open: dp
  _7_Segment_Display u_7_segment_display_6 (
    .g(display_control_1_months_ssd_g), .f(display_control_1_months_ssd_f),
    .a(display_control_1_months_ssd_a), .b(display_control_1_months_ssd_b),
    .e(display_control_1_months_ssd_e), .d(display_control_1_months_ssd_d), .c(display_control_1_months_ssd_c));  // open: dp
  _7_Segment_Display u_7_segment_display_7 (
    .g(display_control_1_tens_month_days_ssd_g), .f(display_control_1_tens_month_days_ssd_f),
    .a(display_control_1_tens_month_days_ssd_a), .b(display_control_1_tens_month_days_ssd_b),
    .e(display_control_1_tens_month_days_ssd_e), .d(display_control_1_tens_month_days_ssd_d),
    .c(display_control_1_tens_month_days_ssd_c));  // open: dp
  _7_Segment_Display u_7_segment_display_8 (
    .g(display_control_1_tens_seconds_ssd_g), .f(display_control_1_tens_seconds_ssd_f),
    .a(display_control_1_tens_seconds_ssd_a), .b(display_control_1_tens_seconds_ssd_b),
    .e(display_control_1_tens_seconds_ssd_e), .d(display_control_1_tens_seconds_ssd_d),
    .c(display_control_1_tens_seconds_ssd_c));  // open: dp
  _7_Segment_Display u_7_segment_display_9 (
    .g(display_control_1_month_days_ssd_g), .f(display_control_1_month_days_ssd_f),
    .a(display_control_1_month_days_ssd_a), .b(display_control_1_month_days_ssd_b),
    .e(display_control_1_month_days_ssd_e), .d(display_control_1_month_days_ssd_d),
    .c(display_control_1_month_days_ssd_c));  // open: dp
  _7_Segment_Display u_7_segment_display_10 (
    .g(display_control_1_seconds_ssd_g), .f(display_control_1_seconds_ssd_f),
    .a(display_control_1_seconds_ssd_a), .b(display_control_1_seconds_ssd_b),
    .e(display_control_1_seconds_ssd_e), .d(display_control_1_seconds_ssd_d),
    .c(display_control_1_seconds_ssd_c));  // open: dp
  display_control display_control_1 (
    .centuries(century), .years(year), .months(month), .day_of_month(month_day), .day_of_week(week_day),
    .hours(hours), .minutes(minutes), .seconds_ssd_a(display_control_1_seconds_ssd_a),
    .seconds_ssd_b(display_control_1_seconds_ssd_b), .seconds_ssd_c(display_control_1_seconds_ssd_c),
    .seconds_ssd_d(display_control_1_seconds_ssd_d), .seconds_ssd_e(display_control_1_seconds_ssd_e),
    .seconds_ssd_f(display_control_1_seconds_ssd_f), .seconds_ssd_g(display_control_1_seconds_ssd_g),
    .tens_seconds_ssd_a(display_control_1_tens_seconds_ssd_a),
    .tens_seconds_ssd_b(display_control_1_tens_seconds_ssd_b),
    .tens_seconds_ssd_c(display_control_1_tens_seconds_ssd_c),
    .tens_seconds_ssd_d(display_control_1_tens_seconds_ssd_d),
    .tens_seconds_ssd_e(display_control_1_tens_seconds_ssd_e),
    .tens_seconds_ssd_f(display_control_1_tens_seconds_ssd_f),
    .tens_seconds_ssd_g(display_control_1_tens_seconds_ssd_g),
    .tens_minutes_ssd_a(display_control_1_tens_minutes_ssd_a),
    .tens_minutes_ssd_b(display_control_1_tens_minutes_ssd_b),
    .tens_minutes_ssd_c(display_control_1_tens_minutes_ssd_c),
    .tens_minutes_ssd_d(display_control_1_tens_minutes_ssd_d),
    .tens_minutes_ssd_e(display_control_1_tens_minutes_ssd_e),
    .tens_minutes_ssd_g(display_control_1_tens_minutes_ssd_g),
    .minutes_ssd_a(display_control_1_minutes_ssd_a), .minutes_ssd_b(display_control_1_minutes_ssd_b),
    .minutes_ssd_c(display_control_1_minutes_ssd_c), .minutes_ssd_d(display_control_1_minutes_ssd_d),
    .minutes_ssd_e(display_control_1_minutes_ssd_e), .minutes_ssd_f(display_control_1_minutes_ssd_f),
    .minutes_ssd_g(display_control_1_minutes_ssd_g), .seconds(seconds),
    .hours_ssd_a(display_control_1_hours_ssd_a), .hours_ssd_b(display_control_1_hours_ssd_b),
    .hours_ssd_c(display_control_1_hours_ssd_c), .hours_ssd_d(display_control_1_hours_ssd_d),
    .hours_ssd_e(display_control_1_hours_ssd_e), .hours_ssd_f(display_control_1_hours_ssd_f),
    .hours_ssd_g(display_control_1_hours_ssd_g), .tens_hours_ssd_a(display_control_1_tens_hours_ssd_a),
    .tens_hours_ssd_b(display_control_1_tens_hours_ssd_b),
    .tens_hours_ssd_c(display_control_1_tens_hours_ssd_c),
    .tens_hours_ssd_d(display_control_1_tens_hours_ssd_d),
    .tens_hours_ssd_e(display_control_1_tens_hours_ssd_e),
    .tens_hours_ssd_f(display_control_1_tens_hours_ssd_f),
    .tens_hours_ssd_g(display_control_1_tens_hours_ssd_g),
    .tens_minutes_ssd_f(display_control_1_tens_minutes_ssd_f),
    .tens_month_days_ssd_a(display_control_1_tens_month_days_ssd_a),
    .tens_month_days_ssd_b(display_control_1_tens_month_days_ssd_b),
    .tens_month_days_ssd_c(display_control_1_tens_month_days_ssd_c),
    .tens_month_days_ssd_d(display_control_1_tens_month_days_ssd_d),
    .tens_month_days_ssd_e(display_control_1_tens_month_days_ssd_e),
    .tens_month_days_ssd_f(display_control_1_tens_month_days_ssd_f),
    .tens_month_days_ssd_g(display_control_1_tens_month_days_ssd_g),
    .month_days_ssd_a(display_control_1_month_days_ssd_a),
    .month_days_ssd_b(display_control_1_month_days_ssd_b),
    .month_days_ssd_c(display_control_1_month_days_ssd_c),
    .month_days_ssd_d(display_control_1_month_days_ssd_d),
    .month_days_ssd_e(display_control_1_month_days_ssd_e),
    .month_days_ssd_f(display_control_1_month_days_ssd_f),
    .month_days_ssd_g(display_control_1_month_days_ssd_g),
    .tens_months_ssd_a(display_control_1_tens_months_ssd_a),
    .tens_months_ssd_b(display_control_1_tens_months_ssd_b),
    .tens_months_ssd_c(display_control_1_tens_months_ssd_c),
    .tens_months_ssd_d(display_control_1_tens_months_ssd_d),
    .tens_months_ssd_e(display_control_1_tens_months_ssd_e),
    .tens_months_ssd_f(display_control_1_tens_months_ssd_f),
    .tens_months_ssd_g(display_control_1_tens_months_ssd_g), .months_ssd_a(display_control_1_months_ssd_a),
    .months_ssd_b(display_control_1_months_ssd_b), .months_ssd_c(display_control_1_months_ssd_c),
    .months_ssd_d(display_control_1_months_ssd_d), .months_ssd_f(display_control_1_months_ssd_f),
    .months_ssd_g(display_control_1_months_ssd_g), .months_ssd_e(display_control_1_months_ssd_e),
    .fast_clk(_4Hz), .adjust_control_reg(adjust_select), .adjust_en(adjust_en),
    .week_day_L0(display_control_1_week_day_l0), .week_day_L1(display_control_1_week_day_l1),
    .week_day_L2(display_control_1_week_day_l2), .week_day_L3(display_control_1_week_day_l3),
    .week_day_L4(display_control_1_week_day_l4), .week_day_L6(display_control_1_week_day_l6),
    .week_day_L7(display_control_1_week_day_l7), .week_day_L8(display_control_1_week_day_l8),
    .week_day_L9(display_control_1_week_day_l9), .week_day_L10(display_control_1_week_day_l10),
    .week_day_L11(display_control_1_week_day_l11), .week_day_L12(display_control_1_week_day_l12),
    .week_day_L13(display_control_1_week_day_l13), .week_day_L14(display_control_1_week_day_l14),
    .week_day_L15(display_control_1_week_day_l15), .week_day_L16(display_control_1_week_day_l16),
    .week_day_L5(display_control_1_week_day_l5));

  // Notes on the sheet:
  //   :
  //   -
endmodule

module clock_conditioning (
  input  clock,
  output _4Hz,
  output half_sec,
  output _1Hz,
  output half_hundreds_seconds,
  output half_tens_seconds,
  output _5_seconds
);

  wire _64Hz, rise_detect_1_delayed, rise_detect_2_delayed, rise_detect_3_delayed;
  wire [2:0] adder_4_out, multiplexer_3_out, tens_sec_counter_2_q;
  wire [4:0] adder_2_out, adder_3_out, hundreds_sec_counter_q, multiplexer_1_out, multiplexer_2_out,
       tens_sec_counter_q;
  wire [20:0] adder_1_out;
  wire [20:1] div_register_q;

  Multiplexer #(.width(5), .enable("false")) multiplexer_1 (
    .in0(adder_2_out), .in1({5{1'b0}}), .out(multiplexer_1_out), .sel(half_hundreds_seconds));
  rise_detect rise_detect_1 (.clk(clock), .D(_64Hz), .delayed(rise_detect_1_delayed));
  Multiplexer #(.width(5), .enable("false")) multiplexer_2 (
    .in0(adder_3_out), .in1({5{1'b0}}), .out(multiplexer_2_out), .sel(half_tens_seconds));
  rise_detect rise_detect_2 (.clk(clock), .D(_64Hz), .delayed(rise_detect_2_delayed));
  Multiplexer #(.width(3), .enable("false")) multiplexer_3 (
    .in0(adder_4_out), .in1(3'b000), .out(multiplexer_3_out), .sel(_5_seconds));
  rise_detect rise_detect_3 (.clk(clock), .D(_1Hz), .delayed(rise_detect_3_delayed));
  Register #(.width(21)) div_register (
    .D(adder_1_out), .Q({div_register_q[20:9], _1Hz, half_sec, _4Hz, div_register_q[5:1], _64Hz}), .clk(clock));  // open: en, clr
  Register #(.width(5)) hundreds_sec_counter (
    .D(multiplexer_1_out), .en(rise_detect_1_delayed), .Q(hundreds_sec_counter_q), .clk(clock));  // open: clr
  Register #(.width(5)) tens_sec_counter (
    .D(multiplexer_2_out), .en(rise_detect_2_delayed), .Q(tens_sec_counter_q), .clk(clock));  // open: clr
  Register #(.width(3)) tens_sec_counter_2 (
    .D(multiplexer_3_out), .en(rise_detect_3_delayed), .Q(tens_sec_counter_2_q), .clk(clock));  // open: clr
  Adder #(.width(21)) adder_1 (
    .a({div_register_q[20:9], _1Hz, half_sec, _4Hz, div_register_q[5:1], _64Hz}), .b({21{1'b0}}),
    .out(adder_1_out), .cin(1'b1));  // open: cout
  Adder #(.width(5)) adder_2 (.a(hundreds_sec_counter_q), .b({5{1'b0}}), .out(adder_2_out), .cin(1'b1));  // open: cout
  Adder #(.width(5)) adder_3 (.a(tens_sec_counter_q), .b({5{1'b0}}), .out(adder_3_out), .cin(1'b1));  // open: cout
  Adder #(.width(3)) adder_4 (.a(tens_sec_counter_2_q), .b(3'b000), .out(adder_4_out), .cin(1'b1));  // open: cout
  Comparator #(.width(5), .mode("unsigned")) comparator_1 (
    .a(hundreds_sec_counter_q), .b(5'b11001), .eq(half_hundreds_seconds));  // open: gt, lt
  Comparator #(.width(5), .mode("unsigned")) comparator_2 (
    .a(tens_sec_counter_q), .b(5'b10100), .eq(half_tens_seconds));  // open: gt, lt
  Comparator #(.width(3), .mode("unsigned")) comparator_3 (
    .a(tens_sec_counter_2_q), .b(3'b101), .eq(_5_seconds));  // open: gt, lt

  // Other names for the same wires on the sheet: clk = clock
endmodule

module time_data (
  input  [6:0] centuries_set,
  input  centuries_set_en,
  input  [6:0] years_set,
  input  years_set_en,
  input  [3:0] months_set,
  input  months_set_en,
  input  [4:0] day_of_month_set,
  input  day_of_month_set_en,
  input  [2:0] day_of_week_set,
  input  day_of_week_set_en,
  input  [4:0] hours_set,
  input  hours_set_en,
  input  [5:0] minutes_set,
  input  minutes_set_en,
  input  [5:0] seconds_set,
  input  seconds_set_en,
  input  clk,
  input  adjust_en,
  input  set,
  input  [2:0] adjust_control_reg,
  output [6:0] centuries_out,
  output [6:0] years_out,
  output [3:0] months_out,
  output [4:0] day_of_month_out,
  output [2:0] day_of_week_out,
  output [4:0] hours_out,
  output [5:0] minutes_out,
  output [5:0] seconds_out
);

  wire and_1_out, and_2_out, fall_detect_1_delayed, fall_detect_2_delayed, fall_detect_3_delayed,
       fall_detect_4_delayed, fall_detect_5_delayed, fall_detect_6_delayed, fall_detect_7_delayed,
       fall_detect_8_delayed;

  and and_1 (and_1_out, ~adjust_control_reg[0], ~adjust_control_reg[1], ~adjust_control_reg[2]);  // AND_Gate
  fall_detect fall_detect_1 (.clk(clk), .D(centuries_set_en), .delayed(fall_detect_1_delayed));
  fall_detect fall_detect_2 (.clk(clk), .D(years_set_en), .delayed(fall_detect_2_delayed));
  fall_detect fall_detect_3 (.clk(clk), .D(months_set_en), .delayed(fall_detect_3_delayed));
  fall_detect fall_detect_4 (.clk(clk), .D(day_of_month_set_en), .delayed(fall_detect_4_delayed));
  fall_detect fall_detect_5 (.clk(clk), .D(day_of_week_set_en), .delayed(fall_detect_5_delayed));
  fall_detect fall_detect_6 (.clk(clk), .D(hours_set_en), .delayed(fall_detect_6_delayed));
  fall_detect fall_detect_7 (.clk(clk), .D(minutes_set_en), .delayed(fall_detect_7_delayed));
  fall_detect fall_detect_8 (.clk(clk), .D(seconds_set_en), .delayed(fall_detect_8_delayed));
  and and_2 (and_2_out, adjust_en, set, and_1_out);
  Register #(.width(7)) centuries (
    .D(centuries_set), .en(fall_detect_1_delayed), .Q(centuries_out), .clk(clk));  // open: clr
  Register #(.width(7)) years (.D(years_set), .en(fall_detect_2_delayed), .Q(years_out), .clk(clk));  // open: clr
  Register #(.width(4)) months (.D(months_set), .en(fall_detect_3_delayed), .Q(months_out), .clk(clk));  // open: clr
  Register #(.width(5)) day_of_month (
    .D(day_of_month_set), .en(fall_detect_4_delayed), .Q(day_of_month_out), .clk(clk));  // open: clr
  Register #(.width(3)) day_of_month_2 (
    .D(day_of_week_set), .en(fall_detect_5_delayed), .Q(day_of_week_out), .clk(clk));  // open: clr
  Register #(.width(5)) hours (.D(hours_set), .en(fall_detect_6_delayed), .Q(hours_out), .clk(clk));  // open: clr
  Register #(.width(6)) minutes (.D(minutes_set), .en(fall_detect_7_delayed), .Q(minutes_out), .clk(clk));  // open: clr
  Register #(.width(6)) seconds (
    .D(seconds_set), .en(fall_detect_8_delayed), .Q(seconds_out), .clk(clk), .clr(and_2_out));
endmodule

module time_advance_logic (
  input  [5:0] seconds,
  input  [5:0] minutes,
  input  [4:0] hours,
  input  [2:0] week_day,
  input  [4:0] day_of_month,
  input  [3:0] months,
  input  [6:0] years,
  input  [6:0] centuries,
  input  adjust_en,
  input  set,
  input  [2:0] adjust_control_reg,
  output [5:0] seconds_set,
  output [5:0] minutes_set,
  output [4:0] hours_set,
  output [2:0] week_day_set,
  output [4:0] day_of_month_set,
  output [3:0] months_set,
  output [6:0] years_set,
  output [6:0] centuries_set,
  output minutes_set_en,
  output hours_set_en,
  output week_day_set_en,
  output day_of_month_set_en,
  output months_set_en,
  output years_set_en,
  output centuries_set_en
);

  wire and_7_out, and_8_out, and_9_out, and_10_out, and_11_out, and_12_out, centuries_adjust,
       days_of_month_loop, decoder_1_out0, decoder_1_out1, decoder_1_out2, decoder_1_out3, decoder_1_out4,
       decoder_1_out5, decoder_1_out6, hours_adjust, hours_loop, is_leap_year, minutes_adjust, minutes_loop,
       month_day_adjust, months_adjust, months_loop, n7bit_equal_99_2__99, seconds_loop, years_adjust,
       years_loop;
  wire [3:0] adder_5_out;
  wire [4:0] adder_3_out, adder_4_out, days_in_month_zero;
  wire [5:0] adder_1_out, adder_2_out;
  wire [6:0] adder_6_out, adder_7_out;

  Decoder #(.select(3), .disabled(0), .enable("false")) decoder_1 (
    .out0(decoder_1_out0), .out1(decoder_1_out1), .out2(decoder_1_out2), .out3(decoder_1_out3),
    .out4(decoder_1_out4), .out5(decoder_1_out5), .out6(decoder_1_out6), .sel(adjust_control_reg));  // open: out7
  Adder #(.width(6)) adder_1 (.a(seconds), .b({6{1'b0}}), .out(adder_1_out), .cin(1'b1));  // open: cout
  Adder #(.width(6)) adder_2 (.a(minutes), .b({6{1'b0}}), .out(adder_2_out), .cin(1'b1));  // open: cout
  Adder #(.width(5)) adder_3 (.a(hours), .b({5{1'b0}}), .out(adder_3_out), .cin(1'b1));  // open: cout
  Adder #(.width(5)) adder_4 (.a(day_of_month), .b({5{1'b0}}), .out(adder_4_out), .cin(1'b1));  // open: cout
  and and_1 (minutes_adjust, adjust_en, set, decoder_1_out1);
  and and_2 (hours_adjust, adjust_en, set, decoder_1_out2);
  and and_3 (month_day_adjust, adjust_en, set, decoder_1_out3);
  and and_4 (months_adjust, adjust_en, set, decoder_1_out4);
  and and_5 (years_adjust, adjust_en, set, decoder_1_out5);
  and and_6 (centuries_adjust, adjust_en, set, decoder_1_out6);
  Adder #(.width(4)) adder_5 (.a(months), .b(4'b0000), .out(adder_5_out), .cin(1'b1));  // open: cout
  Adder #(.width(7)) adder_6 (.a(years), .b({7{1'b0}}), .out(adder_6_out), .cin(1'b1));  // open: cout
  Adder #(.width(7)) adder_7 (.a(centuries), .b({7{1'b0}}), .out(adder_7_out), .cin(1'b1));  // open: cout
  _6bit_equal_59 u_6bit_equal_59_1 (._6bit_in(seconds), ._59(seconds_loop));
  _6bit_equal_59 u_6bit_equal_59_2 (._6bit_in(minutes), ._59(minutes_loop));
  _5bit_equal_23 u_5bit_equal_23_1 (._5bit_in(hours), ._23(hours_loop));
  Comparator #(.width(5), .mode("unsigned")) comparator_1 (
    .a(day_of_month), .b(days_in_month_zero), .eq(days_of_month_loop));  // open: gt, lt
  _4bit_equal_12 u_4bit_equal_12_1 (._7bit_in(months), ._99(months_loop));
  _7bit_equal_99 u_7bit_equal_99_1 (._7bit_in(years), ._99(years_loop));
  _7bit_equal_99 u_7bit_equal_99_2 (._7bit_in(centuries), ._99(n7bit_equal_99_2__99));
  Multiplexer #(.width(6), .enable("false")) multiplexer_1 (
    .in0(adder_1_out), .in1({6{1'b0}}), .out(seconds_set), .sel(seconds_loop));
  Multiplexer #(.width(6), .enable("false")) multiplexer_2 (
    .in0(adder_2_out), .in1({6{1'b0}}), .out(minutes_set), .sel(minutes_loop));
  Multiplexer #(.width(5), .enable("false")) multiplexer_3 (
    .in0(adder_3_out), .in1({5{1'b0}}), .out(hours_set), .sel(hours_loop));
  Multiplexer #(.width(5), .enable("false")) multiplexer_4 (
    .in0(adder_4_out), .in1({5{1'b0}}), .out(day_of_month_set), .sel(days_of_month_loop));
  Multiplexer #(.width(4), .enable("false")) multiplexer_5 (
    .in0(adder_5_out), .in1(4'b0000), .out(months_set), .sel(months_loop));
  Multiplexer #(.width(7), .enable("false")) multiplexer_6 (
    .in0(adder_6_out), .in1({7{1'b0}}), .out(years_set), .sel(years_loop));
  Multiplexer #(.width(7), .enable("false")) multiplexer_7 (
    .in0(adder_7_out), .in1({7{1'b0}}), .out(centuries_set), .sel(n7bit_equal_99_2__99));
  and and_7 (and_7_out, ~adjust_en, seconds_loop);  // AND_Gate
  and and_8 (and_8_out, ~adjust_en, minutes_loop);  // AND_Gate
  and and_9 (and_9_out, ~adjust_en, hours_loop);  // AND_Gate
  and and_10 (and_10_out, ~adjust_en, days_of_month_loop);  // AND_Gate
  and and_11 (and_11_out, ~adjust_en, months_loop);  // AND_Gate
  and and_12 (and_12_out, ~adjust_en, years_loop);  // AND_Gate
  or or_1 (minutes_set_en, minutes_adjust, and_7_out);
  or or_2 (hours_set_en, hours_adjust, and_8_out);
  or or_3 (day_of_month_set_en, month_day_adjust, and_9_out);
  or or_4 (months_set_en, months_adjust, and_10_out);
  or or_5 (years_set_en, years_adjust, and_11_out);
  or or_6 (centuries_set_en, centuries_adjust, and_12_out);
  ROM #(.addrWidth(3), .dataWidth(3)) rom_1 (.addr(week_day), .data(week_day_set));  // open: sel
  days_in_month days_in_month_1 (.is_leap_year(is_leap_year), .month(months), .days_in_month(days_in_month_zero));
  is_leap_year is_leap_year_1 (.year(years), .centuries(centuries), .is_leap_year(is_leap_year));

  assign week_day_set_en = day_of_month_set_en;

  // Other names for the same wires on the sheet: cur_century[6:0] = centuries; cur_month[3:0] = months;
  //   cur_year[6:0] = years

  // Notes on the sheet:
  //   contents of rom_1 (hex, n*v repeats v):
  //   1 2 3 4 5 6
endmodule

module _6bit_equal_59 (
  input  [5:0] _6bit_in,
  output _59
);

  Comparator #(.width(6), .mode("unsigned")) comparator_1 (.a(_6bit_in), .b(6'b111011), .eq(_59));  // open: gt, lt
endmodule

module _5bit_equal_23 (
  input  [4:0] _5bit_in,
  output _23
);

  Comparator #(.width(5), .mode("unsigned")) comparator_1 (.a(_5bit_in), .b(5'b10111), .eq(_23));  // open: gt, lt
endmodule

module _4bit_equal_12 (
  input  [3:0] _7bit_in,
  output _99
);

  Comparator #(.width(4), .mode("unsigned")) comparator_1 (.a(_7bit_in), .b(4'b1011), .eq(_99));  // open: gt, lt
endmodule

module _7bit_equal_99 (
  input  [6:0] _7bit_in,
  output _99
);

  Comparator #(.width(7), .mode("unsigned")) comparator_1 (.a(_7bit_in), .b(7'b1100011), .eq(_99));  // open: gt, lt
endmodule

module days_in_month (
  input  is_leap_year,
  input  [3:0] month,
  output [4:0] days_in_month
);

  wire and_2_out, and_3_out, and_4_out, and_5_out, and_6_out, D0, D1, not_1_out, not_2_out, not_3_out,
       not_4_out, or_1_out;

  // Probe on month
  not not_1 (not_1_out, month[0]);
  not not_2 (not_2_out, month[1]);
  not not_3 (not_3_out, month[2]);
  not not_4 (not_4_out, month[3]);
  and and_1 (D1, month[0], not_3_out, not_2_out, not_4_out);
  and and_2 (and_2_out, month[0], month[1], not_3_out, not_4_out);
  and and_3 (and_3_out, month[0], not_2_out, month[2], not_4_out);
  and and_4 (and_4_out, month[3], not_2_out, not_3_out, not_1_out);
  and and_5 (and_5_out, not_1_out, month[1], not_3_out, month[3]);
  and and_6 (and_6_out, is_leap_year, D1);
  or or_1 (or_1_out, and_2_out, and_3_out, and_4_out, and_5_out);
  or or_2 (D0, and_6_out, or_1_out);
  xnor xnor_1 (days_in_month[0], D0, D1);
  not not_5 (days_in_month[1], D1);
  // Probe on {3'b111, days_in_month[1:0]}

  assign days_in_month[4:2] = 3'b111;
endmodule

module is_leap_year (
  input  [6:0] year,
  input  [6:0] centuries,
  output is_leap_year
);

  // Probe on year
  // Probe on centuries
  ROM #(.addrWidth(14), .dataWidth(1)) rom_1 (.addr({centuries, year}), .data(is_leap_year));  // open: sel

  // Notes on the sheet:
  //   contents of rom_1 (hex, n*v repeats v):
  //   1 0 0 0 1 0 0 0 1 0 0 0 1 0 0 0 1 0 0 0 1 0 0 0 1 0 0 0 1 0 0 0 1 0 0 0 1 0 0 0 1 0 0 0 1 0 0 0 1 0
  //   0 0 1 0 0 0 1 0 0 0 1 0 0 0 1 0 0 0 1 0 0 0 1 0 0 0 1 0 0 0 1 0 0 0 1 0 0 0 1 0 0 0 1 0 0 0 1 7*0 1
  //   0 0 0 1 0 0 0 1 0 0 0 1 0 0 0 1 0 0 0 1 7*0 1 0 0 0 1 0 0 0 1 0 0 0 1 0 0 0 1 0 0 0 1 0 0 0 1 0 0 0
  //   1 0 0 0 1 0 0 0 1 0 0 0 1 0 0 0 1 0 0 0 1 0 0 0 1 0 0 0 1 0 0 0 1 0 0 0 1 0 0 0 1 0 0 0 1 0 0 0 1 0
  //   0 0 1 0 0 0 1 0 0 0 1 0 0 0 1 7*0 1 0 0 0 1 0 0 0 1 0 0 0 1 0 0 0 1 0 0 0 1 7*0 1 0 0 0 1 0 0 0 1 0
  //   0 0 1 0 0 0 1 0 0 0 1 0 0 0 1 0 0 0 1 0 0 0 1 0 0 0 1 0 0 0 1 0 0 0 1 0 0 0 1 0 0 0 1 0 0 0 1 0 0 0
  //   1 0 0 0 1 0 0 0 1 0 0 0 1 0 0 0 1 0 0 0 1 0 0 0 1 0 0 0 1 0 0 0 1 7*0 1 0 0 0 1 0 0 0 1 0 0 0 1 0 0
  //   0 1 0 0 0 1 7*0 1 0 0 0 1 0 0 0 1 0 0 0 1 0 0 0 1 0 0 0 1 0 0 0 1 0 0 0 1 0 0 0 1 0 0 0 1 0 0 0 1 0
  //   0 0 1 0 0 0 1 0 0 0 1 0 0 0 1 0 0 0 1 0 0 0 1 0 0 0 1 0 0 0 1 0 0 0 1 0 0 0 1 0 0 0 1 0 0 0 1 0 0 0
  //   1 0 0 0 1 0 0 0 1 0 0 0 1 0 0 0 1 0 0 0 1 0 0 0 1 0 0 0 1 0 0 0 1 0 0 0 1 0 0 0 1 0 0 0 1 0 0 0 1 0
  //   0 0 1 0 0 0 1 0 0 0 1 0 0 0 1 0 0 0 1 0 0 0 1 0 0 0 1 0 0 0 1 0 0 0 1 0 0 0 1 0 0 0 1 0 0 0 1 0 0 0
  //   1 0 0 0 1 0 0 0 1 0 0 0 1 0 0 0 1 0 0 0 1 0 0 0 1 0 0 0 1 7*0 1 0 0 0 1 0 0 0 1 0 0 0 1 0 0 0 1 0 0
  //   0 1 7*0 1 0 0 0 1 0 0 0 1 0 0 0 1 0 0 0 1 0 0 0 1 0 0 0 1 0 0 0 1 0 0 0 1 0 0 0 1 0 0 0 1 0 0 0 1 0
  //   0 0 1 0 0 0 1 0 0 0 1 0 0 0 1 0 0 0 1 0 0 0 1 0 0 0 1 0 0 0 1 0 0 0 1 0 0 0 1 0 0 0 1 0 0 0 1 7*0 1
  //   0 0 0 1 0 0 0 1 0 0 0 1 0 0 0 1 0 0 0 1 7*0 1 0 0 0 1 0 0 0 1 0 0 0 1 0 0 0 1 0 0 0 1 0 0 0 1 0 0 0
  //   1 0 0 0 1 0 0 0 1 0 0 0 1 0 0 0 1 0 0 0 1 0 0 0 1 0 0 0 1 0 0 0 1 0 0 0 1 0 0 0 1 0 0 0 1 0 0 0 1 0
  //   0 0 1 0 0 0 1 0 0 0 1 0 0 0 1 7*0 1 0 0 0 1 0 0 0 1 0 0 0 1 0 0 0 1 0 0 0 1 7*0 1 0 0 0 1 0 0 0 1 0
  //   0 0 1 0 0 0 1 0 0 0 1 0 0 0 1 0 0 0 1 0 0 0 1 0 0 0 1 0 0 0 1 0 0 0 1 0 0 0 1 0 0 0 1 0 0 0 1 0 0 0
  //   1 0 0 0 1 0 0 0 1 0 0 0 1 0 0 0 1 0 0 0 1 0 0 0 1 0 0 0 1 0 0 0 1 0 0 0 1 0 0 0 1 0 0 0 1 0 0 0 1 0
  //   0 0 1 0 0 0 1 0 0 0 1 0 0 0 1 0 0 0 1 0 0 0 1 0 0 0 1 0 0 0 1 0 0 0 1 0 0 0 1 0 0 0 1 0 0 0 1 0 0 0
  //   1 0 0 0 1 0 0 0 1 0 0 0 1 0 0 0 1 0 0 0 1 0 0 0 1 0 0 0 1 0 0 0 1 0 0 0 1 0 0 0 1 0 0 0 1 0 0 0 1 0
  //   0 0 1 0 0 0 1 0 0 0 1 7*0 1 0 0 0 1 0 0 0 1 0 0 0 1 0 0 0 1 0 0 0 1 7*0 1 0 0 0 1 0 0 0 1 0 0 0 1 0
  //   0 0 1 0 0 0 1 0 0 0 1 0 0 0 1 0 0 0 1 0 0 0 1 0 0 0 1 0 0 0 1 0 0 0 1 0 0 0 1 0 0 0 1 0 0 0 1 0 0 0
  //   1 0 0 0 1 0 0 0 1 0 0 0 1 0 0 0 1 0 0 0 1 0 0 0 1 0 0 0 1 7*0 1 0 0 0 1 0 0 0 1 0 0 0 1 0 0 0 1 0 0
  //   0 1 7*0 1 0 0 0 1 0 0 0 1 0 0 0 1 0 0 0 1 0 0 0 1 0 0 0 1 0 0 0 1 0 0 0 1 0 0 0 1 0 0 0 1 0 0 0 1 0
  //   0 0 1 0 0 0 1 0 0 0 1 0 0 0 1 0 0 0 1 0 0 0 1 0 0 0 1 0 0 0 1 0 0 0 1 0 0 0 1 0 0 0 1 0 0 0 1 7*0 1
  //   0 0 0 1 0 0 0 1 0 0 0 1 0 0 0 1 0 0 0 1 7*0 1 0 0 0 1 0 0 0 1 0 0 0 1 0 0 0 1 0 0 0 1 0 0 0 1 0 0 0
  //   1 0 0 0 1 0 0 0 1 0 0 0 1 0 0 0 1 0 0 0 1 0 0 0 1 0 0 0 1 0 0 0 1 0 0 0 1 0 0 0 1 0 0 0 1 0 0 0 1 0
  //   0 0 1 0 0 0 1 0 0 0 1 0 0 0 1 0 0 0 1 0 0 0 1 0 0 0 1 0 0 0 1 0 0 0 1 0 0 0 1 0 0 0 1 0 0 0 1 0 0 0
  //   1 0 0 0 1 0 0 0 1 0 0 0 1 0 0 0 1 0 0 0 1 0 0 0 1 0 0 0 1 0 0 0 1 0 0 0 1 0 0 0 1 0 0 0 1 0 0 0 1 0
  //   0 0 1 0 0 0 1 0 0 0 1 0 0 0 1 0 0 0 1 0 0 0 1 0 0 0 1 0 0 0 1 0 0 0 1 0 0 0 1 0 0 0 1 7*0 1 0 0 0 1
  //   0 0 0 1 0 0 0 1 0 0 0 1 0 0 0 1 7*0 1 0 0 0 1 0 0 0 1 0 0 0 1 0 0 0 1 0 0 0 1 0 0 0 1 0 0 0 1 0 0 0
  //   1 0 0 0 1 0 0 0 1 0 0 0 1 0 0 0 1 0 0 0 1 0 0 0 1 0 0 0 1 0 0 0 1 0 0 0 1 0 0 0 1 0 0 0 1 0 0 0 1 0
  //   0 0 1 0 0 0 1 0 0 0 1 7*0 1 0 0 0 1 0 0 0 1 0 0 0 1 0 0 0 1 0 0 0 1 7*0 1 0 0 0 1 0 0 0 1 0 0 0 1 0
  //   0 0 1 0 0 0 1 0 0 0 1 0 0 0 1 0 0 0 1 0 0 0 1 0 0 0 1 0 0 0 1 0 0 0 1 0 0 0 1 0 0 0 1 0 0 0 1 0 0 0
  //   1 0 0 0 1 0 0 0 1 0 0 0 1 0 0 0 1 0 0 0 1 0 0 0 1 0 0 0 1 7*0 1 0 0 0 1 0 0 0 1 0 0 0 1 0 0 0 1 0 0
  //   0 1 7*0 1 0 0 0 1 0 0 0 1 0 0 0 1 0 0 0 1 0 0 0 1 0 0 0 1 0 0 0 1 0 0 0 1 0 0 0 1 0 0 0 1 0 0 0 1 0
  //   0 0 1 0 0 0 1 0 0 0 1 0 0 0 1 0 0 0 1 0 0 0 1 0 0 0 1 0 0 0 1 0 0 0 1 0 0 0 1 0 0 0 1 0 0 0 1 0 0 0
  //   1 0 0 0 1 0 0 0 1 0 0 0 1 0 0 0 1 0 0 0 1 0 0 0 1 0 0 0 1 0 0 0 1 0 0 0 1 0 0 0 1 0 0 0 1 0 0 0 1 0
  //   0 0 1 0 0 0 1 0 0 0 1 0 0 0 1 0 0 0 1 0 0 0 1 0 0 0 1 0 0 0 1 0 0 0 1 0 0 0 1 0 0 0 1 0 0 0 1 0 0 0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
endmodule

module BCD_to_7Seg (
  input  [3:0] BDC_in,
  output a_out,
  output b_out,
  output c_out,
  output d_out,
  output e_out,
  output f_out,
  output g_out
);

  wire A_n, and_1_out, and_2_out, and_3_out, and_4_out, and_5_out, and_6_out, and_7_out, and_8_out,
       and_9_out, and_10_out, and_11_out, and_12_out, and_13_out, and_14_out, and_15_out, and_16_out, B_n,
       C_n, D_n;

  and and_1 (and_1_out, BDC_in[1], BDC_in[0]);
  or or_1 (b_out, B_n, and_1_out, and_2_out);
  and and_2 (and_2_out, D_n, C_n);
  and and_3 (and_3_out, BDC_in[2], BDC_in[0]);
  and and_4 (and_4_out, B_n, D_n);
  not not_1 (D_n, BDC_in[0]);
  not not_2 (C_n, BDC_in[1]);
  not not_3 (B_n, BDC_in[2]);
  not not_4 (A_n, BDC_in[3]);
  or or_2 (a_out, BDC_in[3], BDC_in[1], and_3_out, and_4_out);
  or or_3 (c_out, BDC_in[2], C_n, BDC_in[0]);
  and and_5 (and_5_out, BDC_in[0], C_n, BDC_in[2]);
  and and_6 (and_6_out, BDC_in[1], B_n);
  and and_7 (and_7_out, B_n, D_n);
  and and_8 (and_8_out, D_n, BDC_in[1]);
  or or_4 (d_out, BDC_in[3], and_5_out, and_6_out, and_7_out, and_8_out);
  _7_Segment_Display u_7_segment_display_1 (
    .g(g_out), .f(f_out), .a(a_out), .b(b_out), .e(e_out), .d(d_out), .c(c_out));  // open: dp
  and and_9 (and_9_out, B_n, D_n);
  or or_5 (e_out, and_9_out, and_10_out);
  and and_10 (and_10_out, D_n, BDC_in[1]);
  and and_11 (and_11_out, D_n, BDC_in[2]);
  and and_12 (and_12_out, BDC_in[2], C_n);
  and and_13 (and_13_out, C_n, D_n);
  or or_6 (f_out, BDC_in[3], and_11_out, and_12_out, and_13_out);
  and and_14 (and_14_out, B_n, BDC_in[1]);
  and and_15 (and_15_out, C_n, BDC_in[2]);
  and and_16 (and_16_out, BDC_in[2], D_n);
  or or_7 (g_out, BDC_in[3], and_14_out, and_15_out, and_16_out);

  // Other names for the same wires on the sheet: a_t = a_out; b_t = b_out; D = BDC_in[0]; C = BDC_in[1];
  //   B = BDC_in[2]; A = BDC_in[3]; c_t = c_out; d_t = d_out; e = e_out; f = f_out; g = g_out
endmodule

module _7bit_to_BCD (
  input  [6:0] _7bit_in,
  output [3:0] LSB_out,
  output [3:0] MSB_out
);

  ROM #(.addrWidth(7)) rom_1 (.addr(_7bit_in), .data({MSB_out, LSB_out}));  // open: sel

  // Notes on the sheet:
  //   contents of rom_1 (hex, n*v repeats v):
  //   0 1 2 3 4 5 6 7 8 9 10 11 12 13 14 15 16 17 18 19 20 21 22 23 24 25 26 27 28 29 30 31 32 33 34 35 36
  //   37 38 39 40 41 42 43 44 45 46 47 48 49 50 51 52 53 54 55 56 57 58 59 60 61 62 63 64 65 66 67 68 69
  //   70 71 72 73 74 75 76 77 78 79 80 81 82 83 84 85 86 87 88 89 90 91 92 93 94 95 96 97 98 29*99
endmodule

module display_control (
  input  [6:0] centuries,
  input  adjust_en,
  input  [2:0] adjust_control_reg,
  input  [3:0] months,
  input  [6:0] years,
  input  [2:0] day_of_week,
  input  [4:0] day_of_month,
  input  [4:0] hours,
  input  [5:0] minutes,
  input  fast_clk,
  input  [5:0] seconds,
  output tens_months_ssd_a,
  output tens_months_ssd_b,
  output tens_months_ssd_c,
  output tens_months_ssd_d,
  output tens_months_ssd_e,
  output tens_months_ssd_f,
  output tens_months_ssd_g,
  output months_ssd_a,
  output months_ssd_b,
  output months_ssd_c,
  output months_ssd_d,
  output months_ssd_e,
  output months_ssd_f,
  output months_ssd_g,
  output tens_month_days_ssd_a,
  output [4:0] week_day_L0,
  output tens_month_days_ssd_b,
  output [4:0] week_day_L1,
  output tens_month_days_ssd_c,
  output [4:0] week_day_L2,
  output tens_month_days_ssd_d,
  output tens_month_days_ssd_e,
  output [4:0] week_day_L3,
  output tens_month_days_ssd_f,
  output [4:0] week_day_L4,
  output tens_month_days_ssd_g,
  output [4:0] week_day_L5,
  output month_days_ssd_a,
  output month_days_ssd_b,
  output [4:0] week_day_L6,
  output month_days_ssd_c,
  output [4:0] week_day_L7,
  output month_days_ssd_d,
  output [4:0] week_day_L8,
  output month_days_ssd_e,
  output month_days_ssd_f,
  output [4:0] week_day_L9,
  output month_days_ssd_g,
  output [4:0] week_day_L10,
  output [4:0] week_day_L11,
  output [4:0] week_day_L12,
  output tens_hours_ssd_a,
  output tens_hours_ssd_b,
  output [4:0] week_day_L13,
  output tens_hours_ssd_c,
  output [4:0] week_day_L14,
  output tens_hours_ssd_d,
  output [4:0] week_day_L15,
  output tens_hours_ssd_e,
  output tens_hours_ssd_f,
  output [4:0] week_day_L16,
  output tens_hours_ssd_g,
  output hours_ssd_a,
  output hours_ssd_b,
  output hours_ssd_c,
  output hours_ssd_d,
  output hours_ssd_e,
  output hours_ssd_f,
  output hours_ssd_g,
  output tens_minutes_ssd_a,
  output tens_minutes_ssd_b,
  output tens_minutes_ssd_c,
  output tens_minutes_ssd_d,
  output tens_minutes_ssd_e,
  output tens_minutes_ssd_f,
  output tens_minutes_ssd_g,
  output minutes_ssd_a,
  output minutes_ssd_b,
  output minutes_ssd_c,
  output minutes_ssd_d,
  output minutes_ssd_e,
  output minutes_ssd_f,
  output minutes_ssd_g,
  output tens_seconds_ssd_a,
  output tens_seconds_ssd_b,
  output tens_seconds_ssd_c,
  output tens_seconds_ssd_d,
  output tens_seconds_ssd_e,
  output tens_seconds_ssd_f,
  output tens_seconds_ssd_g,
  output seconds_ssd_a,
  output seconds_ssd_b,
  output seconds_ssd_c,
  output seconds_ssd_d,
  output seconds_ssd_e,
  output seconds_ssd_f,
  output seconds_ssd_g
);

  wire centuries_adjust, decoder_1_out0, decoder_1_out1, decoder_1_out2, decoder_1_out3, decoder_1_out4,
       decoder_1_out5, decoder_1_out6, hours_adjust, minutes_adjust, month_day_adjust, months_adjust,
       seconds_adjust, years_adjust;
  wire [3:0] adder_1_out;
  wire [4:0] adder_2_out;
  wire [6:0] bit_extender_1_out, bit_extender_2_out, bit_extender_3_out, bit_extender_4_out,
       bit_extender_5_out;

  Adder #(.width(4)) adder_1 (.a(months), .b(4'b0000), .out(adder_1_out), .cin(1'b1));  // open: cout
  Adder #(.width(5)) adder_2 (.a(day_of_month), .b({5{1'b0}}), .out(adder_2_out), .cin(1'b1));  // open: cout
  assign bit_extender_1_out = {{3{1'b0}}, adder_1_out};  // Bit_Extender bit_extender_1
  assign bit_extender_2_out = {{2{1'b0}}, adder_2_out};  // Bit_Extender bit_extender_2
  assign bit_extender_3_out = {{2{1'b0}}, hours};  // Bit_Extender bit_extender_3
  assign bit_extender_4_out = {{1{1'b0}}, minutes};  // Bit_Extender bit_extender_4
  assign bit_extender_5_out = {{1{1'b0}}, seconds};  // Bit_Extender bit_extender_5
  timedata_to_SSD timedata_to_ssd_1 (
    .adjust_enable(fast_clk), .fast_clk(months_adjust), .timedata_in(bit_extender_1_out),
    .tens_ssd_a(tens_months_ssd_a), .tens_ssd_b(tens_months_ssd_b), .tens_ssd_c(tens_months_ssd_c),
    .tens_ssd_d(tens_months_ssd_d), .tens_ssd_e(tens_months_ssd_e), .tens_ssd_f(tens_months_ssd_f),
    .tens_ssd_g(tens_months_ssd_g), .ssd_a(months_ssd_a), .ssd_b(months_ssd_b), .ssd_c(months_ssd_c),
    .ssd_d(months_ssd_d), .ssd_e(months_ssd_e), .ssd_f(months_ssd_f), .ssd_g(months_ssd_g));
  timedata_to_SSD timedata_to_ssd_2 (
    .adjust_enable(fast_clk), .fast_clk(month_day_adjust), .timedata_in(bit_extender_2_out),
    .tens_ssd_a(tens_month_days_ssd_a), .tens_ssd_b(tens_month_days_ssd_b),
    .tens_ssd_c(tens_month_days_ssd_c), .tens_ssd_d(tens_month_days_ssd_d),
    .tens_ssd_e(tens_month_days_ssd_e), .tens_ssd_f(tens_month_days_ssd_f),
    .tens_ssd_g(tens_month_days_ssd_g), .ssd_a(month_days_ssd_a), .ssd_b(month_days_ssd_b),
    .ssd_c(month_days_ssd_c), .ssd_d(month_days_ssd_d), .ssd_e(month_days_ssd_e), .ssd_f(month_days_ssd_f),
    .ssd_g(month_days_ssd_g));
  timedata_to_SSD timedata_to_ssd_3 (
    .adjust_enable(fast_clk), .fast_clk(hours_adjust), .timedata_in(bit_extender_3_out),
    .tens_ssd_a(tens_hours_ssd_a), .tens_ssd_b(tens_hours_ssd_b), .tens_ssd_c(tens_hours_ssd_c),
    .tens_ssd_d(tens_hours_ssd_d), .tens_ssd_e(tens_hours_ssd_e), .tens_ssd_f(tens_hours_ssd_f),
    .tens_ssd_g(tens_hours_ssd_g), .ssd_a(hours_ssd_a), .ssd_b(hours_ssd_b), .ssd_c(hours_ssd_c),
    .ssd_d(hours_ssd_d), .ssd_e(hours_ssd_e), .ssd_f(hours_ssd_f), .ssd_g(hours_ssd_g));
  timedata_to_SSD timedata_to_ssd_4 (
    .adjust_enable(fast_clk), .fast_clk(minutes_adjust), .timedata_in(bit_extender_4_out),
    .tens_ssd_a(tens_minutes_ssd_a), .tens_ssd_b(tens_minutes_ssd_b), .tens_ssd_c(tens_minutes_ssd_c),
    .tens_ssd_d(tens_minutes_ssd_d), .tens_ssd_e(tens_minutes_ssd_e), .tens_ssd_f(tens_minutes_ssd_f),
    .tens_ssd_g(tens_minutes_ssd_g), .ssd_a(minutes_ssd_a), .ssd_b(minutes_ssd_b), .ssd_c(minutes_ssd_c),
    .ssd_d(minutes_ssd_d), .ssd_e(minutes_ssd_e), .ssd_f(minutes_ssd_f), .ssd_g(minutes_ssd_g));
  timedata_to_SSD timedata_to_ssd_5 (
    .adjust_enable(fast_clk), .fast_clk(seconds_adjust), .timedata_in(bit_extender_5_out),
    .tens_ssd_a(tens_seconds_ssd_a), .tens_ssd_b(tens_seconds_ssd_b), .tens_ssd_c(tens_seconds_ssd_c),
    .tens_ssd_d(tens_seconds_ssd_d), .tens_ssd_e(tens_seconds_ssd_e), .tens_ssd_f(tens_seconds_ssd_f),
    .tens_ssd_g(tens_seconds_ssd_g), .ssd_a(seconds_ssd_a), .ssd_b(seconds_ssd_b), .ssd_c(seconds_ssd_c),
    .ssd_d(seconds_ssd_d), .ssd_e(seconds_ssd_e), .ssd_f(seconds_ssd_f), .ssd_g(seconds_ssd_g));
  Decoder #(.select(3), .disabled(0), .enable("false")) decoder_1 (
    .out0(decoder_1_out0), .out1(decoder_1_out1), .out2(decoder_1_out2), .out3(decoder_1_out3),
    .out4(decoder_1_out4), .out5(decoder_1_out5), .out6(decoder_1_out6), .sel(adjust_control_reg));  // open: out7
  and and_1 (seconds_adjust, adjust_en, decoder_1_out0);
  and and_2 (minutes_adjust, adjust_en, decoder_1_out1);
  and and_3 (hours_adjust, adjust_en, decoder_1_out2);
  and and_4 (month_day_adjust, adjust_en, decoder_1_out3);
  and and_5 (months_adjust, adjust_en, decoder_1_out4);
  and and_6 (years_adjust, adjust_en, decoder_1_out5);
  and and_7 (centuries_adjust, adjust_en, decoder_1_out6);
  week_day_display_control week_day_display_control_1 (
    .weed_day(day_of_week), .week_day_L0(week_day_L0), .week_day_L1(week_day_L1), .week_day_L2(week_day_L2),
    .week_day_L3(week_day_L3), .week_day_L4(week_day_L4), .week_day_L6(week_day_L6),
    .week_day_L7(week_day_L7), .week_day_L8(week_day_L8), .week_day_L9(week_day_L9),
    .week_day_L10(week_day_L10), .week_day_L12(week_day_L12), .week_day_L13(week_day_L13),
    .week_day_L14(week_day_L14), .week_day_L15(week_day_L15), .week_day_L16(week_day_L16),
    .week_day_L5(week_day_L5), .week_day_L11(week_day_L11));
endmodule

module rise_detect (
  input  clk,
  input  D,
  output delayed
);

  wire d_ff_1_q, d_ff_2_q, not_1_out;

  D_Flip_Flop d_ff_1 (.clk(clk), .D(D), .Q(d_ff_1_q));  // open: Qn, preset, en, reset
  D_Flip_Flop d_ff_2 (.clk(clk), .D(d_ff_1_q), .Q(d_ff_2_q));  // open: Qn, preset, en, reset
  not not_1 (not_1_out, d_ff_2_q);
  and and_1 (delayed, not_1_out, d_ff_1_q);
endmodule

module long_press_detect (
  input  D,
  input  reset,
  input  clk,
  output press_detected
);

  Counter #(.width(7), .max('h7f)) counter_1 (
    .count(D), .carry(press_detected), .clk(clk), .clr(reset));  // open: load, D, Q
endmodule

module fall_detect (
  input  clk,
  input  D,
  output delayed
);

  wire d_ff_1_q, d_ff_2_q, not_1_out;

  D_Flip_Flop d_ff_1 (.clk(clk), .D(D), .Q(d_ff_1_q));  // open: Qn, preset, en, reset
  D_Flip_Flop d_ff_2 (.clk(clk), .D(d_ff_1_q), .Q(d_ff_2_q));  // open: Qn, preset, en, reset
  not not_1 (not_1_out, d_ff_1_q);
  and and_1 (delayed, d_ff_2_q, not_1_out);
endmodule

module state_control (
  input  clk,
  input  set,
  input  mode,
  input  adjust,
  output [2:0] adjust_state_reg,
  output mode_encode,
  output set_out,
  output time_set_mode
);

  wire adjust_reset, and_1_out, long_press_detect_1_press_detected, next_mode, not_1_out;

  not not_1 (not_1_out, time_set_mode);
  T_Flip_Flop t_ff_1 (.clk(clk), .T(next_mode), .Q(mode_encode), .en(not_1_out));  // open: Qn, preset, reset
  rise_detect rise_detect_1 (.clk(clk), .D(set), .delayed(set_out));
  rise_detect rise_detect_2 (.clk(clk), .D(mode), .delayed(next_mode));
  rise_detect rise_detect_3 (.clk(clk), .D(adjust), .delayed(adjust_reset));
  long_press_detect long_press_detect_1 (
    .D(adjust), .clk(clk), .press_detected(long_press_detect_1_press_detected), .reset(adjust_reset));
  and and_1 (and_1_out, next_mode, time_set_mode);
  S_R_Flip_Flop s_r_ff_1 (
    .S(long_press_detect_1_press_detected), .clk(clk), .R(adjust_reset), .Q(time_set_mode));  // open: Qn, preset, reset, en
  Counter #(.width(3), .max('h6)) counter_1 (
    .count(and_1_out), .Q(adjust_state_reg), .clk(clk), .clr(adjust_reset));  // open: load, D, carry

  // Other names for the same wires on the sheet: time_set_mode_en = time_set_mode
endmodule

module timedata_to_SSD (
  input  adjust_enable,
  input  fast_clk,
  input  [6:0] timedata_in,
  output tens_ssd_a,
  output tens_ssd_b,
  output tens_ssd_c,
  output tens_ssd_d,
  output tens_ssd_e,
  output tens_ssd_f,
  output tens_ssd_g,
  output ssd_a,
  output ssd_b,
  output ssd_c,
  output ssd_d,
  output ssd_e,
  output ssd_f,
  output ssd_g
);

  wire bcd_to_7seg_1_a_out, bcd_to_7seg_1_b_out, bcd_to_7seg_1_c_out, bcd_to_7seg_1_d_out,
       bcd_to_7seg_1_e_out, bcd_to_7seg_1_f_out, bcd_to_7seg_1_g_out, bcd_to_7seg_2_a_out,
       bcd_to_7seg_2_b_out, bcd_to_7seg_2_c_out, bcd_to_7seg_2_d_out, bcd_to_7seg_2_e_out,
       bcd_to_7seg_2_f_out, bcd_to_7seg_2_g_out, nand_1_out;
  wire [3:0] n7bit_to_bcd_1_lsb_out, n7bit_to_bcd_1_msb_out;

  _7bit_to_BCD u_7bit_to_bcd_1 (
    .MSB_out(n7bit_to_bcd_1_msb_out), .LSB_out(n7bit_to_bcd_1_lsb_out), ._7bit_in(timedata_in));
  BCD_to_7Seg bcd_to_7seg_1 (
    .BDC_in(n7bit_to_bcd_1_msb_out), .a_out(bcd_to_7seg_1_a_out), .b_out(bcd_to_7seg_1_b_out),
    .c_out(bcd_to_7seg_1_c_out), .d_out(bcd_to_7seg_1_d_out), .e_out(bcd_to_7seg_1_e_out),
    .f_out(bcd_to_7seg_1_f_out), .g_out(bcd_to_7seg_1_g_out));
  BCD_to_7Seg bcd_to_7seg_2 (
    .BDC_in(n7bit_to_bcd_1_lsb_out), .a_out(bcd_to_7seg_2_a_out), .b_out(bcd_to_7seg_2_b_out),
    .c_out(bcd_to_7seg_2_c_out), .d_out(bcd_to_7seg_2_d_out), .e_out(bcd_to_7seg_2_e_out),
    .f_out(bcd_to_7seg_2_f_out), .g_out(bcd_to_7seg_2_g_out));
  nand nand_1 (nand_1_out, adjust_enable, fast_clk);
  Transistor #(.\type ("n")) transistor_1 (.in(bcd_to_7seg_1_a_out), .out(tens_ssd_a), .gate(nand_1_out));
  Transistor #(.\type ("n")) transistor_2 (.in(bcd_to_7seg_1_b_out), .out(tens_ssd_b), .gate(nand_1_out));
  Transistor #(.\type ("n")) transistor_3 (.in(bcd_to_7seg_1_c_out), .out(tens_ssd_c), .gate(nand_1_out));
  Transistor #(.\type ("n")) transistor_4 (.in(bcd_to_7seg_1_d_out), .out(tens_ssd_d), .gate(nand_1_out));
  Transistor #(.\type ("n")) transistor_5 (.in(bcd_to_7seg_1_e_out), .out(tens_ssd_e), .gate(nand_1_out));
  Transistor #(.\type ("n")) transistor_6 (.in(bcd_to_7seg_1_f_out), .out(tens_ssd_f), .gate(nand_1_out));
  Transistor #(.\type ("n")) transistor_7 (.in(bcd_to_7seg_1_g_out), .out(tens_ssd_g), .gate(nand_1_out));
  Transistor #(.\type ("n")) transistor_8 (.in(bcd_to_7seg_2_a_out), .out(ssd_a), .gate(nand_1_out));
  Transistor #(.\type ("n")) transistor_9 (.in(bcd_to_7seg_2_b_out), .out(ssd_b), .gate(nand_1_out));
  Transistor #(.\type ("n")) transistor_10 (.in(bcd_to_7seg_2_c_out), .out(ssd_c), .gate(nand_1_out));
  Transistor #(.\type ("n")) transistor_11 (.in(bcd_to_7seg_2_d_out), .out(ssd_d), .gate(nand_1_out));
  Transistor #(.\type ("n")) transistor_12 (.in(bcd_to_7seg_2_e_out), .out(ssd_e), .gate(nand_1_out));
  Transistor #(.\type ("n")) transistor_13 (.in(bcd_to_7seg_2_f_out), .out(ssd_f), .gate(nand_1_out));
  Transistor #(.\type ("n")) transistor_14 (.in(bcd_to_7seg_2_g_out), .out(ssd_g), .gate(nand_1_out));
endmodule

module week_day_display_control (
  input  [2:0] weed_day,
  output [4:0] week_day_L0,
  output [4:0] week_day_L1,
  output [4:0] week_day_L2,
  output [4:0] week_day_L3,
  output [4:0] week_day_L4,
  output [4:0] week_day_L5,
  output [4:0] week_day_L6,
  output [4:0] week_day_L7,
  output [4:0] week_day_L8,
  output [4:0] week_day_L9,
  output [4:0] week_day_L10,
  output [4:0] week_day_L11,
  output [4:0] week_day_L12,
  output [4:0] week_day_L13,
  output [4:0] week_day_L14,
  output [4:0] week_day_L15,
  output [4:0] week_day_L16
);

  ROM #(.addrWidth(3), .dataWidth(5)) rom_1 (.addr(weed_day), .data(week_day_L0));  // open: sel
  ROM #(.addrWidth(3), .dataWidth(5)) rom_2 (.addr(weed_day), .data(week_day_L1));  // open: sel
  ROM #(.addrWidth(3), .dataWidth(5)) rom_3 (.addr(weed_day), .data(week_day_L2));  // open: sel
  ROM #(.addrWidth(3), .dataWidth(5)) rom_4 (.addr(weed_day), .data(week_day_L3));  // open: sel
  ROM #(.addrWidth(3), .dataWidth(5)) rom_5 (.addr(weed_day), .data(week_day_L4));  // open: sel
  ROM #(.addrWidth(3), .dataWidth(5)) rom_6 (.addr(weed_day), .data(week_day_L6));  // open: sel
  ROM #(.addrWidth(3), .dataWidth(5)) rom_7 (.addr(weed_day), .data(week_day_L7));  // open: sel
  ROM #(.addrWidth(3), .dataWidth(5)) rom_8 (.addr(weed_day), .data(week_day_L8));  // open: sel
  ROM #(.addrWidth(3), .dataWidth(5)) rom_9 (.addr(weed_day), .data(week_day_L9));  // open: sel
  ROM #(.addrWidth(3), .dataWidth(5)) rom_10 (.addr(weed_day), .data(week_day_L10));  // open: sel
  ROM #(.addrWidth(3), .dataWidth(5)) rom_11 (.addr(weed_day), .data(week_day_L12));  // open: sel
  ROM #(.addrWidth(3), .dataWidth(5)) rom_12 (.addr(weed_day), .data(week_day_L13));  // open: sel
  ROM #(.addrWidth(3), .dataWidth(5)) rom_13 (.addr(weed_day), .data(week_day_L14));  // open: sel
  ROM #(.addrWidth(3), .dataWidth(5)) rom_14 (.addr(weed_day), .data(week_day_L15));  // open: sel
  ROM #(.addrWidth(3), .dataWidth(5)) rom_15 (.addr(weed_day), .data(week_day_L16));  // open: sel
  DotMatrix #(.matrixcols(17), .matrixrows(5)) dotmatrix_1 (
    .col0(week_day_L0), .col1(week_day_L1), .col2(week_day_L2), .col3(week_day_L3), .col4(week_day_L4),
    .col5({5{1'b0}}), .col6(week_day_L6), .col7(week_day_L7), .col8(week_day_L8), .col9(week_day_L9),
    .col10(week_day_L10), .col11({5{1'b0}}), .col12(week_day_L12), .col13(week_day_L13),
    .col14(week_day_L14), .col15(week_day_L15), .col16(week_day_L16));

  assign week_day_L5 = {5{1'b0}};
  assign week_day_L11 = {5{1'b0}};

  // Notes on the sheet:
  //   contents of rom_1 (hex, n*v repeats v):
  //   9 1f 10 1e 10 1f 9
  //   contents of rom_2 (hex, n*v repeats v):
  //   15 8 10 1 10 14 15
  //   contents of rom_3 (hex, n*v repeats v):
  //   15 4 1f e 1f 14 15
  //   contents of rom_4 (hex, n*v repeats v):
  //   15 8 10 1 10 10 15
  //   contents of rom_5 (hex, n*v repeats v):
  //   12 1f 10 1e 10 10 12
  //   contents of rom_6 (hex, n*v repeats v):
  //   1e e 1e 1f 1f 1f f
  //   contents of rom_7 (hex, n*v repeats v):
  //   1 11 1 15 4 14 14
  //   contents of rom_8 (hex, n*v repeats v):
  //   1 11 1 15 4 14 14
  //   contents of rom_9 (hex, n*v repeats v):
  //   1 11 1 15 4 16 14
  //   contents of rom_10 (hex, n*v repeats v):
  //   1e e 1e 11 1f 9 f
  //   contents of rom_11 (hex, n*v repeats v):
  //   4*1f 1e 0 10
  //   contents of rom_12 (hex, n*v repeats v):
  //   8 8 15 11 1 11 10
  //   contents of rom_13 (hex, n*v repeats v):
  //   4 4 15 11 1 1f 1f
  //   contents of rom_14 (hex, n*v repeats v):
  //   2 2 15 11 1 11 10
  //   contents of rom_15 (hex, n*v repeats v):
  //   1f 1f 11 e 1e 0 10
endmodule

module timer (
  input  reset,
  input  clk,
  input  half_hundredth_seconds,
  output [6:0] hundredths_seconds_timer,
  output [6:0] seconds_timer,
  output [6:0] minutes_timer
);

  wire comparator_1_eq, comparator_2_eq, comparator_3_eq, fall_detect_1_delayed, fall_detect_2_delayed,
       fall_detect_3_delayed, hundredths_zero, not_3_out, seconds_zero;
  wire [6:0] adder_1_out, adder_2_out, adder_3_out, multiplexer_1_out, multiplexer_2_out, multiplexer_3_out;

  Adder #(.width(7)) adder_1 (
    .a(hundredths_seconds_timer), .b({7{1'b0}}), .out(adder_1_out), .cin(1'b1));  // open: cout
  fall_detect fall_detect_1 (.clk(clk), .D(half_hundredth_seconds), .delayed(fall_detect_1_delayed));
  Adder #(.width(7)) adder_2 (.a(seconds_timer), .b({7{1'b0}}), .out(adder_2_out), .cin(1'b1));  // open: cout
  fall_detect fall_detect_2 (.clk(clk), .D(hundredths_zero), .delayed(fall_detect_2_delayed));
  Adder #(.width(7)) adder_3 (.a(minutes_timer), .b({7{1'b0}}), .out(adder_3_out), .cin(1'b1));  // open: cout
  fall_detect fall_detect_3 (.clk(clk), .D(seconds_zero), .delayed(fall_detect_3_delayed));
  Comparator #(.width(7), .mode("unsigned")) comparator_1 (
    .a(hundredths_seconds_timer), .b(7'b1100011), .eq(comparator_1_eq));  // open: gt, lt
  not not_1 (hundredths_zero, comparator_1_eq);
  Comparator #(.width(7), .mode("unsigned")) comparator_2 (
    .a(seconds_timer), .b(7'b1100011), .eq(comparator_2_eq));  // open: gt, lt
  not not_2 (seconds_zero, comparator_2_eq);
  Comparator #(.width(7), .mode("unsigned")) comparator_3 (
    .a(minutes_timer), .b(7'b1100011), .eq(comparator_3_eq));  // open: gt, lt
  not not_3 (not_3_out, comparator_3_eq);
  Multiplexer #(.width(7), .enable("false")) multiplexer_1 (
    .in0({7{1'b0}}), .in1(adder_1_out), .out(multiplexer_1_out), .sel(hundredths_zero));
  Multiplexer #(.width(7), .enable("false")) multiplexer_2 (
    .in0({7{1'b0}}), .in1(adder_2_out), .out(multiplexer_2_out), .sel(seconds_zero));
  Multiplexer #(.width(7), .enable("false")) multiplexer_3 (
    .in0({7{1'b0}}), .in1(adder_3_out), .out(multiplexer_3_out), .sel(not_3_out));
  Register #(.width(7)) hundredth_sec (
    .D(multiplexer_1_out), .Q(hundredths_seconds_timer), .clk(clk), .clr(reset));  // open: en
  Register #(.width(7)) sec (
    .D(multiplexer_2_out), .en(fall_detect_2_delayed), .Q(seconds_timer), .clk(clk), .clr(reset));
  Register #(.width(7)) sec_2 (
    .D(multiplexer_3_out), .en(fall_detect_3_delayed), .Q(minutes_timer), .clk(clk), .clr(reset));
endmodule
